# Fritzing sketch AnalogSignalGenerator (saved by Fritzing 0.9.3b)
circuit board: 11cm x 10cm

parts:
  Data_Lines = double row female pin header, 40 pins [form="♀ (female)"]
  SW1 = DIP Switch 8 Position [package=dipswitch-08]
  SW2 = DIP Switch 8 Position [package=dipswitch-08]
  RP* = Resistor [tolerance=±5% resistance=1M package="0805 [SMD]"]
  RP*_2 = Resistor [tolerance=±5% resistance=1M package="0805 [SMD]"]
  RP*_3 = Resistor [tolerance=±5% resistance=1M package="0805 [SMD]"]
  RP*_4 = Resistor [tolerance=±5% resistance=1M package="0805 [SMD]"]
  RP*_5 = Resistor [tolerance=±5% resistance=1M package="0805 [SMD]"]
  RP*_6 = Resistor [tolerance=±5% resistance=1M package="0805 [SMD]"]
  RP*_7 = Resistor [tolerance=±5% resistance=1M package="0805 [SMD]"]
  RP*_8 = Resistor [tolerance=±5% resistance=1M package="0805 [SMD]"]
  RP*_9 = Resistor [tolerance=±5% resistance=1M package="0805 [SMD]"]
  RP*_10 = Resistor [tolerance=±5% resistance=1M package="0805 [SMD]"]
  RP*_11 = Resistor [tolerance=±5% resistance=1M package="0805 [SMD]"]
  RP*_12 = Resistor [tolerance=±5% resistance=1M package="0805 [SMD]"]
  RP*_13 = Resistor [tolerance=±5% resistance=1M package="0805 [SMD]"]
  RP*_14 = Resistor [tolerance=±5% resistance=1M package="0805 [SMD]"]
  RP*_15 = Resistor [tolerance=±5% resistance=1M package="0805 [SMD]"]
  RP*_16 = Resistor [tolerance=±5% resistance=1M package="0805 [SMD]"]
  IC3 = SOIC-14 [chip_label=CD4081BM96 package=SO]
  Sys_1B1 = smd LED [color="Green (560nm)" package="1206 [SMD]"]
  Sys_3B1 = smd LED [color="Green (560nm)" package="1206 [SMD]"]
  Sys_2B1 = smd LED [color="Green (560nm)" package="1206 [SMD]"]
  Sys_4B1 = smd LED [color="Green (560nm)" package="1206 [SMD]"]
  Sys_4A1 = smd LED [color="Green (560nm)" package="1206 [SMD]"]
  Sys_3A1 = smd LED [color="Green (560nm)" package="1206 [SMD]"]
  Sys_2A1 = smd LED [color="Green (560nm)" package="1206 [SMD]"]
  Sys_1A1 = smd LED [color="Green (560nm)" package="1206 [SMD]"]
  Power_B1 = smd LED [color="Orange (620nm)" package="1206 [SMD]"]
  Power_A1 = smd LED [color="Orange (620nm)" package="1206 [SMD]"]
  RL10 = Resistor [tolerance=±5% resistance=60 package="0805 [SMD]"]
  RL9 = Resistor [tolerance=±5% resistance=60 package="0805 [SMD]"]
  RL8 = Resistor [tolerance=±5% resistance=60 package="0805 [SMD]"]
  RL7 = Resistor [tolerance=±5% resistance=60 package="0805 [SMD]"]
  RL6 = Resistor [tolerance=±5% resistance=60 package="0805 [SMD]"]
  RL5 = Resistor [tolerance=±5% resistance=60 package="0805 [SMD]"]
  RL4 = Resistor [tolerance=±5% resistance=60 package="0805 [SMD]"]
  RL3 = Resistor [tolerance=±5% resistance=60 package="0805 [SMD]"]
  RL2 = Resistor [tolerance=±5% resistance=60 package="0805 [SMD]"]
  RL1 = Resistor [tolerance=±5% resistance=60 package="0805 [SMD]"]
  R2 = Resistor [tolerance=±0.1% resistance=10k package="0805 [SMD]"]
  C2 = Ceramic Capacitor [capacitance=15nF package="0805 [SMD, multilayer]"]
  C2_2 = Ceramic Capacitor [capacitance=15nF package="0805 [SMD, multilayer]"]
  R2_2 = Resistor [tolerance=±0.1% resistance=10k package="0805 [SMD]"]
  R1 = Resistor [tolerance=±0.1% resistance=10k package="0805 [SMD]"]
  C1 = Ceramic Capacitor [capacitance=10nF package="0805 [SMD, multilayer]"]
  R1_2 = Resistor [tolerance=±0.1% resistance=10k package="0805 [SMD]"]
  C1_2 = Ceramic Capacitor [capacitance=10nF package="0805 [SMD, multilayer]"]
  R1_3 = Resistor [tolerance=±0.1% resistance=10k package="0805 [SMD]"]
  R1_4 = Resistor [tolerance=±0.1% resistance=10k package="0805 [SMD]"]
  R2_3 = Resistor [tolerance=±0.1% resistance=10k package="0805 [SMD]"]
  C1_3 = Ceramic Capacitor [capacitance=10nF package="0805 [SMD, multilayer]"]
  C1_4 = Ceramic Capacitor [capacitance=10nF package="0805 [SMD, multilayer]"]
  BUF2 = Ceramic Capacitor [capacitance=100nF voltage=30V package="0805 [SMD, multilayer]"]
  C2_3 = Ceramic Capacitor [capacitance=15nF package="0805 [SMD, multilayer]"]
  R2_4 = Resistor [tolerance=±0.1% resistance=10k package="0805 [SMD]"]
  C2_4 = Ceramic Capacitor [capacitance=15nF package="0805 [SMD, multilayer]"]
  Teensy1 = Teensy 3.1
  Teensy2 = Teensy 3.1
  IC1 = SOIC-14 [chip_label=TLC084 part_number=595-TLC084CDR package=SO]
  Analog_Out = double row female pin header, 10 pins [form="♀ (female)"]
  IC2 = SOIC-14 [chip_label=TLC084 part_number=595-TLC084CDR package=SO]
  BUF4 = Ceramic Capacitor [capacitance=100nF voltage=30V package="0805 [SMD, multilayer]"]
  C2_5 = Ceramic Capacitor [capacitance=15nF package="0805 [SMD, multilayer]"]
  R2_5 = Resistor [tolerance=±0.1% resistance=10k package="0805 [SMD]"]
  C1_5 = Ceramic Capacitor [capacitance=10nF package="0805 [SMD, multilayer]"]
  C2_6 = Ceramic Capacitor [capacitance=15nF package="0805 [SMD, multilayer]"]
  R2_6 = Resistor [tolerance=±0.1% resistance=10k package="0805 [SMD]"]
  C1_6 = Ceramic Capacitor [capacitance=10nF package="0805 [SMD, multilayer]"]
  R2_7 = Resistor [tolerance=±0.1% resistance=10k package="0805 [SMD]"]
  C2_7 = Ceramic Capacitor [capacitance=15nF package="0805 [SMD, multilayer]"]
  C1_7 = Ceramic Capacitor [capacitance=10nF package="0805 [SMD, multilayer]"]
  R2_8 = Resistor [tolerance=±0.1% resistance=10k package="0805 [SMD]"]
  C2_8 = Ceramic Capacitor [capacitance=15nF package="0805 [SMD, multilayer]"]
  C1_8 = Ceramic Capacitor [capacitance=10nF package="0805 [SMD, multilayer]"]
  R1_5 = Resistor [tolerance=±0.1% resistance=10k package="0805 [SMD]"]
  R1_6 = Resistor [tolerance=±0.1% resistance=10k package="0805 [SMD]"]
  R1_7 = Resistor [tolerance=±0.1% resistance=10k package="0805 [SMD]"]
  R1_8 = Resistor [tolerance=±0.1% resistance=10k package="0805 [SMD]"]
  Analog_In_1 = female pin header, 4 pins [form="♀ (female)"]
  Analog_In_2 = female pin header, 4 pins [form="♀ (female)"]
  IC4 = IC, DIP package, 20 pins [chip_label=CD74HCT688EE4]
  IC5 = IC, DIP package, 20 pins [chip_label=CD74HCT688EE4]
  Power_Supply = double row female pin header, 40 pins [form="♀ (female)"]
  BUF9 = Ceramic Capacitor [capacitance=100nF package="0805 [SMD, multilayer]"]
  BUF8 = Ceramic Capacitor [capacitance=10µF voltage=10V package="0805 [SMD, multilayer]"]
  BUF7 = Ceramic Capacitor [capacitance=100nF package="0805 [SMD, multilayer]"]
  BUF6 = Ceramic Capacitor [capacitance=10µF package="0805 [SMD, multilayer]"]
  BUF1 = Ceramic Capacitor [capacitance=100nF package="0603 [SMD, multilayer]"]
  BUF10 = Ceramic Capacitor [capacitance=100nF package="0805 [SMD, multilayer]"]
  BUF11 = Ceramic Capacitor [capacitance=100nF package="0805 [SMD, multilayer]"]
  RP2 = Resistor [tolerance=±5% resistance=1.5k package="0805 [SMD]"]
  RP3 = Resistor [tolerance=±5% resistance=1.5k package="0805 [SMD]"]
  RP1 = Resistor [tolerance=±5% resistance=1.5k package="0805 [SMD]"]
  BUF3 = Ceramic Capacitor [capacitance=6.8µF voltage=10V package="0805 [SMD, multilayer]"]
  BUF5 = Ceramic Capacitor [capacitance=6.8µF voltage=10V package="0805 [SMD, multilayer]"]

nets (from the pcb view):
  N1: Data_Lines.pin1, Data_Lines.pin40, IC3.5, IC3.9
  N2: Data_Lines.pin3, Data_Lines.pin38, IC4.pin9, IC5.pin3
  N3: Data_Lines.pin4, Data_Lines.pin37, IC4.pin7, IC5.pin5
  N4: Data_Lines.pin5, Data_Lines.pin36, IC4.pin5, IC5.pin7
  N5: Data_Lines.pin6, Data_Lines.pin35, IC4.pin3, IC5.pin9
  N6: Data_Lines.pin7, Data_Lines.pin34, IC4.pin12, IC5.pin12
  N7: Data_Lines.pin8, Data_Lines.pin33, IC4.pin14, IC5.pin14
  N8: Data_Lines.pin9, Data_Lines.pin32, IC4.pin16, IC5.pin16
  N9: Data_Lines.pin15, Data_Lines.pin26, Teensy1.A4/D18, Teensy2.A4/D18, RP3.Pin_1
  N10: Data_Lines.pin16, Data_Lines.pin25, Teensy1.A5/D19, Teensy2.A5/D19, RP2.Pin_1
  N11: Data_Lines.pin17, Data_Lines.pin24, IC4.pin18, IC5.pin18
  N12: Data_Lines.pin18, Data_Lines.pin23, Teensy1.D13, Teensy2.D13, RP1.Pin_1
  N13: Data_Lines.pin19, Data_Lines.pin22, Teensy1.D12, Teensy2.D12
  VIN: SW1.1, SW1.2, SW1.3, SW1.4, SW1.5, SW1.6, SW1.7, SW1.8, SW2.1, SW2.2, SW2.3, SW2.4, SW2.5, SW2.6, SW2.7, SW2.8, IC3.14, BUF2.1, Teensy1.Vin, Teensy2.Vin, IC1.4, IC2.4, BUF4.1, IC4.pin20, IC5.pin20, Power_Supply.pin17, Power_Supply.pin18, Power_Supply.pin19, Power_Supply.pin20, Power_Supply.pin21, Power_Supply.pin22, Power_Supply.pin23, Power_Supply.pin24, BUF9.1, BUF8.1, BUF7.1, BUF6.1, BUF1.0, BUF10.0, BUF11.0, RP2.Pin_0, RP3.Pin_0, RP1.Pin_0, BUF3.1, BUF5.1
  N14: SW1.9, RP*_10.Pin_0, IC5.pin17
  N15: SW1.10, RP*_11.Pin_0, IC5.pin15
  N16: SW1.11, RP*_13.Pin_0, IC5.pin13
  N17: SW1.12, RP*_12.Pin_0, IC5.pin11
  N18: SW1.13, RP*_14.Pin_0, IC5.pin8
  N19: SW1.14, RP*_9.Pin_0, IC5.pin6
  N20: SW1.15, RP*_16.Pin_0, IC5.pin4
  N21: SW1.16, RP*_15.Pin_0, IC5.pin2
  N22: SW2.9, RP*_8.Pin_0, IC4.pin17
  N23: SW2.10, RP*_7.Pin_0, IC4.pin15
  N24: SW2.11, RP*_6.Pin_0, IC4.pin13
  N25: SW2.12, RP*.Pin_0, IC4.pin11
  N26: SW2.13, RP*_2.Pin_0, IC4.pin2
  N27: SW2.14, RP*_3.Pin_0, IC4.pin4
  N28: SW2.15, RP*_4.Pin_0, IC4.pin6
  N29: SW2.16, RP*_5.Pin_0, IC4.pin8
  N30: RP*.Pin_1, RP*_2.Pin_1, RP*_3.Pin_1, RP*_4.Pin_1, RP*_5.Pin_1, RP*_6.Pin_1, RP*_7.Pin_1, RP*_8.Pin_1, RP*_9.Pin_1, RP*_10.Pin_1, RP*_11.Pin_1, RP*_12.Pin_1, RP*_13.Pin_1, RP*_14.Pin_1, RP*_15.Pin_1, RP*_16.Pin_1, Sys_1B1.cathode, Sys_3B1.cathode, Sys_2B1.cathode, Sys_4B1.cathode, Sys_4A1.cathode, Sys_3A1.cathode, Sys_2A1.cathode, Sys_1A1.cathode, Power_B1.cathode, Power_A1.cathode, C2.0, C2_2.1, C2_3.0, C2_4.1, C2_5.1, C2_6.0, C2_7.0, C2_8.1, IC4.pin1, IC4.pin10, Power_Supply.pin35, BUF11.1
  N31: IC3.4, Teensy1.D10
  N32: IC3.6, IC5.pin19
  GND: IC3.7, Teensy1.GND, Teensy2.GND, IC5.pin1, IC5.pin10, Power_Supply.pin4, Power_Supply.pin5, Power_Supply.pin6, BUF9.0, BUF8.0, BUF7.0, BUF6.0, BUF1.1, BUF10.1
  N33: IC3.8, IC4.pin19
  N34: IC3.10, Teensy2.D10
  N35: Sys_1B1.anode, RL7.Pin_0
  N36: Sys_3B1.anode, RL9.Pin_0
  N37: Sys_2B1.anode, RL8.Pin_0
  N38: Sys_4B1.anode, RL10.Pin_0
  N39: Sys_4A1.anode, RL5.Pin_0
  N40: Sys_3A1.anode, RL4.Pin_0
  N41: Sys_2A1.anode, RL3.Pin_0
  N42: Sys_1A1.anode, RL2.Pin_0
  N43: Power_B1.anode, RL6.Pin_0
  N44: Power_A1.anode, RL1.Pin_0
  N45: RL10.Pin_1, Teensy2.A9/D23
  N46: RL9.Pin_1, Teensy2.A8/D22
  N47: RL8.Pin_1, Teensy2.A7/D21
  N48: RL7.Pin_1, Teensy2.D9
  N49: RL6.Pin_1, Teensy2.3V3
  N50: RL5.Pin_1, Teensy1.A9/D23
  N51: RL4.Pin_1, Teensy1.A8/D22
  N52: RL3.Pin_1, Teensy1.A7/D21
  N53: RL2.Pin_1, Teensy1.D9
  N54: RL1.Pin_1, Teensy1.3V3
  N55: R2.Pin_0, R1.Pin_1, C1_2.0
  N56: R2.Pin_1, C2.1, IC1.10
  N57: C2_2.0, R2_2.Pin_1, IC1.12
  N58: R2_2.Pin_0, C1.0, R1_2.Pin_1
  N59: R1.Pin_0, Teensy1.D3
  N60: C1.1, IC1.13, IC1.14, Analog_Out.pin1
  N61: R1_2.Pin_0, Teensy1.D4
  N62: C1_2.1, IC1.8, IC1.9, Analog_Out.pin2
  N63: R1_3.Pin_0, Teensy1.D5
  N64: R1_3.Pin_1, R2_3.Pin_0, C1_3.0
  N65: R1_4.Pin_0, Teensy1.D6
  N66: R1_4.Pin_1, C1_4.0, R2_4.Pin_0
  N67: R2_3.Pin_1, C2_4.0, IC1.3
  N68: C1_3.1, IC1.1, IC1.2, Analog_Out.pin4
  N69: C1_4.1, IC1.6, IC1.7, Analog_Out.pin3
  N70: BUF2.0, IC1.11, Analog_Out.pin6, IC2.11, BUF4.0, Power_Supply.pin38, Power_Supply.pin39, Power_Supply.pin40, BUF3.0, BUF5.0
  N71: C2_3.1, R2_4.Pin_1, IC1.5
  N72: Teensy1.A0/D14, Analog_In_1.pin4
  N73: Teensy1.A1/D15, Analog_In_1.pin3
  N74: Teensy1.A2/D16, Analog_In_1.pin2
  N75: Teensy1.A3/D17, Analog_In_1.pin1
  N76: Teensy1.A6/D20, Teensy2.A6/D20, Analog_Out.pin5
  N77: Teensy2.D3, R1_8.Pin_0
  N78: Teensy2.D4, R1_7.Pin_0
  N79: Teensy2.D5, R1_6.Pin_0
  N80: Teensy2.D6, R1_5.Pin_0
  N81: Teensy2.A0/D14, Analog_In_2.pin4
  N82: Teensy2.A1/D15, Analog_In_2.pin3
  N83: Teensy2.A2/D16, Analog_In_2.pin2
  N84: Teensy2.A3/D17, Analog_In_2.pin1
  N85: Analog_Out.pin7, IC2.13, IC2.14, C1_7.0
  N86: Analog_Out.pin8, IC2.8, IC2.9, C1_8.0
  N87: Analog_Out.pin9, IC2.6, IC2.7, C1_5.1
  N88: Analog_Out.pin10, IC2.1, IC2.2, C1_6.0
  N89: IC2.3, C2_6.1, R2_6.Pin_1
  N90: IC2.5, C2_5.0, R2_5.Pin_0
  N91: IC2.10, R2_8.Pin_0, C2_8.0
  N92: IC2.12, R2_7.Pin_0, C2_7.1
  N93: R2_5.Pin_1, C1_5.0, R1_5.Pin_1
  N94: R2_6.Pin_0, C1_6.1, R1_6.Pin_1
  N95: R2_7.Pin_1, C1_7.1, R1_7.Pin_1
  N96: R2_8.Pin_1, C1_8.1, R1_8.Pin_1

notes:
  E-MSB-LSB
  (c) 2015 Andreas Tarnowsky
  1
  Broadcast
  I2C Pullup
  2
  3
  4
  5
  6
  7
  SDA
  SCL
  CS
  CLK
  DATA

custom parts:
  Teensy 3.1: The Teensy is a complete USB-based microcontoller development system, in a very small footprint, capable of implementing many types of projects. All programming is done via the USB port. No special programmer is needed, only a standard micro-USB cable and a PC or Macintosh with a USB port. It has a USB keyboard/mouse/joystick emulation stack and can be programmed through Arduino IDE.
