# Fritzing sketch DisplayBreakout (saved by Fritzing 0.9.3b)
circuit board: 6.5cm x 4cm
breadboards: 1

parts:
  Up = Pushbutton [package="[THT]"]
  Down = Pushbutton [package="[THT]"]
  Back = Pushbutton [package="[THT]"]
  Select = Pushbutton [package="[THT]"]
  OLED = 128x32 I2C Monochrome OLED Display
  Com = double row male pin header, 16 pins [form="♂ (male)"]

nets:
  N1: Up.Pin_1, Up.Pin_2, Down.Pin_1, Down.Pin_2, Back.Pin_1, Back.Pin_2, Select.Pin_1, Select.Pin_2, OLED.GND, Com.pin7, Com.pin8, Com.pin9, Com.pin10
  N2: Up.Pin_3, Up.Pin_4, Com.pin5
  N3: Down.Pin_3, Down.Pin_4, Com.pin6
  N4: Back.Pin_3, Back.Pin_4, Com.pin12
  N5: Select.Pin_3, Select.Pin_4, Com.pin11
  N6: OLED.SDA, Com.pin3
  N7: OLED.SCL, Com.pin14
  N8: OLED.RST, Com.pin4
  N9: OLED.3.3V, Com.pin2, Com.pin15
  N10: OLED.VIN, Com.pin1, Com.pin16
