# Fritzing sketch HighVoltageAmplifier (saved by Fritzing 0.9.3b)
circuit board: 11cm x 10cm
breadboards: 1

parts:
  IC5 = SOIC-14 [chip_label=SN74HC04 part_number=SN74HC04 package=SO]
  IC4 = SO16 [chip_label=SI8645BB-B-IS1 part_number=SI8645BB package=SO]
  IC1 = SOIC-14 [chip_label=FAN73933MX package=SO]
  DC1 = DCDC ROE-0505S
  DC2 = DCDC ROE-0505S
  IC1_2 = SOIC-14 [chip_label=FAN73933MX package=SO]
  R4 = Resistor [tolerance=±5% resistance=220 package="0805 [SMD]"]
  R1 = Resistor [tolerance=±5% resistance=220 package="0805 [SMD]"]
  R2 = Resistor [tolerance=±5% resistance=220 package="0805 [SMD]"]
  R5 = Resistor [tolerance=±5% resistance=220 package="0805 [SMD]"]
  R3 = Resistor [tolerance=±5% resistance=220 package="0805 [SMD]"]
  R6 = Resistor [tolerance=±5% resistance=220 package="0805 [SMD]"]
  C2 = Ceramic Capacitor [capacitance=0.47µF voltage=25V part_number="C2012X7R1E474K125AA [1907325]" package="0805 [SMD, multilayer]"]
  R4_2 = Resistor [tolerance=±5% resistance=220 package="0805 [SMD]"]
  R1_2 = Resistor [tolerance=±5% resistance=220 package="0805 [SMD]"]
  C27 = Ceramic Capacitor [capacitance=100nF package="0805 [SMD, multilayer]"]
  C28 = Ceramic Capacitor [capacitance=100nF package="0805 [SMD, multilayer]"]
  D1 = Rectifier Diode [part_number=EGL41G-E3/96 package="Melf DO-213 AA [SMD]"]
  R2_2 = Resistor [tolerance=±5% resistance=220 package="0805 [SMD]"]
  R5_2 = Resistor [tolerance=±5% resistance=220 package="0805 [SMD]"]
  R3_2 = Resistor [tolerance=±5% resistance=220 package="0805 [SMD]"]
  R6_2 = Resistor [tolerance=±5% resistance=220 package="0805 [SMD]"]
  C2_2 = Ceramic Capacitor [capacitance=0.47µF voltage=25V part_number="C2012X7R1E474K125AA [1907325]" package="0805 [SMD, multilayer]"]
  Data_Lines = double row female pin header, 40 pins [form="♀ (female)"]
  Power_Supply = double row female pin header, 40 pins [form="♀ (female)"]
  J14 = male pin header, 3 pins [form="♂ (male)"]
  J15 = male pin header, 3 pins [form="♂ (male)"]
  Gen_4 = smd LED [color="Green (560nm)" package="1206 [SMD]"]
  Gen_3 = smd LED [color="Green (560nm)" package="1206 [SMD]"]
  Gen_2 = smd LED [color="Green (560nm)" package="1206 [SMD]"]
  Gen_1 = smd LED [color="Green (560nm)" package="1206 [SMD]"]
  Power = smd LED [color="Orange (620nm)" package="1206 [SMD]"]
  R8 = Resistor [tolerance=±5% resistance=220 package="0805 [SMD]"]
  R8_2 = Resistor [tolerance=±5% resistance=220 package="0805 [SMD]"]
  R8_3 = Resistor [tolerance=±5% resistance=220 package="0805 [SMD]"]
  R8_4 = Resistor [tolerance=±5% resistance=220 package="0805 [SMD]"]
  R8_5 = Resistor [tolerance=±5% resistance=220 package="0805 [SMD]"]
  Teensy_3_2 = Teensy 3.1 [part_number="PJRC Teensy 3.2"]
  DIP1_Address = DIP Switch 8 Position [part_number=DIP1 package=dipswitch-08]
  R44 = Resistor [tolerance=±5% resistance=1M package="0805 [SMD]"]
  R45 = Resistor [tolerance=±5% resistance=1M package="0805 [SMD]"]
  RP*1 = Resistor [tolerance=±5% resistance=1M package="0805 [SMD]"]
  R46 = Resistor [tolerance=±5% resistance=1M package="0805 [SMD]"]
  R47 = Resistor [tolerance=±5% resistance=1M package="0805 [SMD]"]
  R48 = Resistor [tolerance=±5% resistance=1M package="0805 [SMD]"]
  R7 = Resistor [tolerance=±5% resistance=1M package="0805 [SMD]"]
  R50 = Resistor [tolerance=±5% resistance=1M package="0805 [SMD]"]
  IC2 = CD74HCT688 SOIC20 [part_number=CD74HCT688]
  CBUF = Ceramic Capacitor [capacitance=100nF package="0805 [SMD, multilayer]"]
  IC3 = SN74LVC1G08 [part_number=SN74LVC1G08 package=sot23-5]
  C3 = RUBYCON Elko
  C1 = Ceramic Capacitor [capacitance=4.7µF voltage=50V part_number="GRM31CR71H475KA12L [1735545]" package="1206 [SMD, multilayer]"]
  C1_2 = Ceramic Capacitor [capacitance=100nF package="1206 [SMD, multilayer]"]
  CBUF_2 = Ceramic Capacitor [capacitance=100nF package="0805 [SMD, multilayer]"]
  CBUF_3 = Ceramic Capacitor [capacitance=100nF package="0805 [SMD, multilayer]"]
  C93 = Ceramic Capacitor [capacitance=100nF package="0805 [SMD, multilayer]"]
  C94 = Ceramic Capacitor [capacitance=100nF package="0805 [SMD, multilayer]"]
  C95 = Ceramic Capacitor [capacitance=100nF package="0805 [SMD, multilayer]"]
  C96 = Ceramic Capacitor [capacitance=100nF package="0805 [SMD, multilayer]"]
  C97 = Ceramic Capacitor [capacitance=100nF package="0805 [SMD, multilayer]"]
  C98 = Ceramic Capacitor [capacitance=100nF package="0805 [SMD, multilayer]"]
  CBUF_4 = Ceramic Capacitor [capacitance=100nF package="0805 [SMD, multilayer]"]
  CBUF_5 = Ceramic Capacitor [capacitance=100nF package="0805 [SMD, multilayer]"]
  C99 = MolexRow
  C100 = MolexRow
  C101 = MolexRow
  IC1_3 = SOIC-14 [chip_label=FAN73933MX package=SO]
  IC1_4 = SOIC-14 [chip_label=FAN73933MX package=SO]
  R2_3 = Resistor [tolerance=±5% resistance=220 package="0805 [SMD]"]
  R2_4 = Resistor [tolerance=±5% resistance=220 package="0805 [SMD]"]
  R5_3 = Resistor [tolerance=±5% resistance=220 package="0805 [SMD]"]
  R5_4 = Resistor [tolerance=±5% resistance=220 package="0805 [SMD]"]
  R3_3 = Resistor [tolerance=±5% resistance=220 package="0805 [SMD]"]
  R3_4 = Resistor [tolerance=±5% resistance=220 package="0805 [SMD]"]
  R6_3 = Resistor [tolerance=±5% resistance=220 package="0805 [SMD]"]
  D1_2 = Rectifier Diode [part_number=EGL41G-E3/96 package="Melf DO-213 AA [SMD]"]
  R6_4 = Resistor [tolerance=±5% resistance=220 package="0805 [SMD]"]
  D1_3 = Rectifier Diode [part_number=EGL41G-E3/96 package="Melf DO-213 AA [SMD]"]
  R4_3 = Resistor [tolerance=±5% resistance=0 package="0805 [SMD]"]
  R4_4 = Resistor [tolerance=±5% resistance=220 package="0805 [SMD]"]
  R1_3 = Resistor [tolerance=±5% resistance=220 package="0805 [SMD]"]
  R1_4 = Resistor [tolerance=±5% resistance=220 package="0805 [SMD]"]
  C1_3 = Ceramic Capacitor [capacitance=4.7µF voltage=50V part_number="GRM31CR71H475KA12L [1735545]" package="1206 [SMD, multilayer]"]
  C1_4 = Ceramic Capacitor [capacitance=4.7µF voltage=50V part_number="GRM31CR71H475KA12L [1735545]" package="1206 [SMD, multilayer]"]
  C2_3 = Ceramic Capacitor [capacitance=0.47µF part_number="C2012X7R1E474K125AA [1907325]" voltage=25V package="0805 [SMD, multilayer]"]
  C2_4 = Ceramic Capacitor [capacitance=0.47µF voltage=25V part_number="C2012X7R1E474K125AA [1907325]" package="0805 [SMD, multilayer]"]
  C107 = Ceramic Capacitor [capacitance=100nF package="0805 [SMD, multilayer]"]
  C109 = Ceramic Capacitor [capacitance=100nF package="0805 [SMD, multilayer]"]
  J16 = male pin header, 2 pins [form="♂ (male)"]
  C120 = Ceramic Capacitor [capacitance=100nF package="0805 [SMD, multilayer]"]
  C121 = Ceramic Capacitor [capacitance=100nF package="0805 [SMD, multilayer]"]
  C122 = Ceramic Capacitor [capacitance=100nF package="0805 [SMD, multilayer]"]
  C123 = Ceramic Capacitor [capacitance=100nF package="0805 [SMD, multilayer]"]
  IC1_5 = SOIC-14 [chip_label=FAN73933MX package=SO]
  IC1_6 = SOIC-14 [chip_label=FAN73933MX package=SO]
  R2_5 = Resistor [tolerance=±5% resistance=220 package="0805 [SMD]"]
  R2_6 = Resistor [tolerance=±5% resistance=220 package="0805 [SMD]"]
  R5_5 = Resistor [tolerance=±5% resistance=220 package="0805 [SMD]"]
  R5_6 = Resistor [tolerance=±5% resistance=220 package="0805 [SMD]"]
  R3_5 = Resistor [tolerance=±5% resistance=220 package="0805 [SMD]"]
  R3_6 = Resistor [tolerance=±5% resistance=220 package="0805 [SMD]"]
  R6_5 = Resistor [tolerance=±5% resistance=220 package="0805 [SMD]"]
  D1_4 = Rectifier Diode [part_number=EGL41G-E3/96 package="Melf DO-213 AA [SMD]"]
  R6_6 = Resistor [tolerance=±5% resistance=220 package="0805 [SMD]"]
  D1_5 = Rectifier Diode [part_number=EGL41G-E3/96 package="Melf DO-213 AA [SMD]"]
  R4_5 = Resistor [tolerance=±5% resistance=220 package="0805 [SMD]"]
  R4_6 = Resistor [tolerance=±5% resistance=220 package="0805 [SMD]"]
  R1_5 = Resistor [tolerance=±5% resistance=220 package="0805 [SMD]"]
  R1_6 = Resistor [tolerance=±5% resistance=220 package="0805 [SMD]"]
  C1_5 = Ceramic Capacitor [capacitance=4.7µF voltage=50V part_number="GRM31CR71H475KA12L [1735545]" package="1206 [SMD, multilayer]"]
  C1_6 = Ceramic Capacitor [capacitance=4.7µF voltage=50V part_number="GRM31CR71H475KA12L [1735545]" package="1206 [SMD, multilayer]"]
  C2_5 = Ceramic Capacitor [capacitance=0.47µF voltage=25V part_number="C2012X7R1E474K125AA [1907325]" package="0805 [SMD, multilayer]"]
  C2_6 = Ceramic Capacitor [capacitance=0.47µF voltage=25V part_number="C2012X7R1E474K125AA [1907325]" package="0805 [SMD, multilayer]"]
  v_R9 = Resistor [tolerance=±5% resistance=220 package="2512 [SMD]"]
  v_R9_2 = Resistor [tolerance=±5% resistance=220 package="2512 [SMD]"]
  R88 = Resistor [tolerance=±5% resistance=220 package="2512 [SMD]"]
  R89 = Resistor [tolerance=±5% resistance=220 package="2512 [SMD]"]
  R90 = Resistor [tolerance=±5% resistance=220 package="2512 [SMD]"]
  R91 = Resistor [tolerance=±5% resistance=220 package="2512 [SMD]"]
  R92 = Resistor [tolerance=±5% resistance=220 package="2512 [SMD]"]
  R93 = Resistor [tolerance=±5% resistance=220 package="2512 [SMD]"]
  IC1_7 = SOIC-14 [chip_label=FAN73933MX package=SO]
  IC1-1 = SOIC-14 [chip_label=FAN73933MX package=SO]
  R1_7 = Resistor [tolerance=±5% resistance=220 package="0805 [SMD]"]
  R1_8 = Resistor [tolerance=±5% resistance=220 package="0805 [SMD]"]
  R6_7 = Resistor [tolerance=±5% resistance=220 package="0805 [SMD]"]
  R5_7 = Resistor [tolerance=±5% resistance=220 package="0805 [SMD]"]
  R6_8 = Resistor [tolerance=±5% resistance=220 package="0805 [SMD]"]
  R5_8 = Resistor [tolerance=±5% resistance=220 package="0805 [SMD]"]
  R3_7 = Resistor [tolerance=±5% resistance=220 package="0805 [SMD]"]
  R2_7 = Resistor [tolerance=±5% resistance=220 package="0805 [SMD]"]
  R3_8 = Resistor [tolerance=±5% resistance=220 package="0805 [SMD]"]
  R2_8 = Resistor [tolerance=±5% resistance=220 package="0805 [SMD]"]
  C2_7 = Ceramic Capacitor [capacitance=0.47µF voltage=25V part_number="C2012X7R1E474K125AA [1907325]" package="0805 [SMD, multilayer]"]
  C2_8 = Ceramic Capacitor [capacitance=0.47µF part_number="C2012X7R1E474K125AA [1907325]" voltage=25V package="0805 [SMD, multilayer]"]
  C1_7 = Ceramic Capacitor [capacitance=4.7µF voltage=50V part_number="GRM31CR71H475KA12L [1735545]" package="1206 [SMD, multilayer]"]
  C1_8 = Ceramic Capacitor [capacitance=4.7µF voltage=50V part_number="GRM31CR71H475KA12L [1735545]" package="1206 [SMD, multilayer]"]
  R4_7 = Resistor [tolerance=±5% resistance=220 package="0805 [SMD]"]
  R4_8 = Resistor [tolerance=±5% resistance=220 package="0805 [SMD]"]
  C102 = MolexRow
  C132 = Ceramic Capacitor [capacitance=100nF package="0805 [SMD, multilayer]"]
  C133 = Ceramic Capacitor [capacitance=100nF package="0805 [SMD, multilayer]"]
  C134 = Ceramic Capacitor [capacitance=100nF package="0805 [SMD, multilayer]"]
  C135 = Ceramic Capacitor [capacitance=100nF package="0805 [SMD, multilayer]"]
  C136 = Ceramic Capacitor [capacitance=100nF package="0805 [SMD, multilayer]"]
  C137 = Ceramic Capacitor [capacitance=100nF package="0805 [SMD, multilayer]"]
  C138 = Ceramic Capacitor [capacitance=100nF package="0805 [SMD, multilayer]"]
  C139 = Ceramic Capacitor [capacitance=100nF package="0805 [SMD, multilayer]"]
  C140 = Ceramic Capacitor [capacitance=100nF package="0805 [SMD, multilayer]"]
  C141 = Ceramic Capacitor [capacitance=100nF package="0805 [SMD, multilayer]"]
  C142 = Ceramic Capacitor [capacitance=100nF package="0805 [SMD, multilayer]"]
  C143 = Ceramic Capacitor [capacitance=100nF package="0805 [SMD, multilayer]"]
  C144 = Ceramic Capacitor [capacitance=100nF package="0805 [SMD, multilayer]"]
  C145 = Ceramic Capacitor [capacitance=100nF package="0805 [SMD, multilayer]"]
  C146 = Ceramic Capacitor [capacitance=100nF package="0805 [SMD, multilayer]"]
  C147 = Ceramic Capacitor [capacitance=100nF package="0805 [SMD, multilayer]"]
  C148 = Ceramic Capacitor [capacitance=100nF package="0805 [SMD, multilayer]"]
  C149 = Ceramic Capacitor [capacitance=100nF package="0805 [SMD, multilayer]"]
  D1_6 = Rectifier Diode [part_number=EGL41G-E3/96 package="Melf DO-213 AA [SMD]"]
  D1_7 = Rectifier Diode [part_number=EGL41G-E3/96 package="Melf DO-213 AA [SMD]"]
  D1_8 = Rectifier Diode [part_number=EGL41G-E3/96 package="Melf DO-213 AA [SMD]"]
  P1 = TrimmpotiDick
  T1 = STN3N40K3 [package=sot223]
  T1_2 = STN3N40K3 [package=sot223]
  T1_3 = STN3N40K3 [package=sot223]
  T1_4 = STN3N40K3 [package=sot223]
  T2 = STN3N40K3 [package=sot223]
  T2_2 = STN3N40K3 [package=sot223]
  T2_3 = STN3N40K3 [package=sot223]
  T1_5 = STN3N40K3 [package=sot223]
  T1_6 = STN3N40K3 [package=sot223]
  T1_7 = STN3N40K3 [package=sot223]
  T2_4 = STN3N40K3 [package=sot223]
  T1_8 = STN3N40K3 [package=sot223]
  T2_5 = STN3N40K3 [package=sot223]
  T2_6 = STN3N40K3 [package=sot223]
  T2_7 = STN3N40K3 [package=sot223]
  T2_8 = STN3N40K3 [package=sot223]

nets (from the pcb view):
  N1: IC5.1, IC4.14, C123.0, C123.1, IC1_5.1, IC1_6.2
  N2: IC5.2, C122.0, C122.1, IC1_5.2, IC1_6.1
  N3: IC5.3, IC4.13, IC1.2, IC1_2.1, C121.0, C121.1
  N4: IC5.4, IC1.1, IC1_2.2, C120.0, C120.1
  N5: IC5.5, IC4.12, C28.0, C28.1, IC1_7.2, IC1-1.1
  N6: IC5.6, C27.0, C27.1, IC1_7.1, IC1-1.2
  N7: IC5.7, IC4.9, IC4.15, IC1.3, IC1.5, DC1.-Vout, DC2.-Vout, IC1_2.3, IC1_2.5, R4.Pin_1, R6.Pin_1, R4_2.Pin_1, R6_2.Pin_0, J15.pin2, C3.plus, C1.0, C1_2.0, C93.0, C94.0, C95.0, C96.0, C97.0, C98.0, CBUF_4.0, CBUF_5.1, IC1_3.3, IC1_3.5, IC1_4.3, IC1_4.5, R6_3.Pin_0, R6_4.Pin_1, R4_3.Pin_1, R4_4.Pin_1, C1_3.0, C1_4.0, IC1_5.3, IC1_5.5, IC1_6.3, IC1_6.5, R6_5.Pin_0, R6_6.Pin_1, R4_5.Pin_1, R4_6.Pin_1, C1_5.0, C1_6.0, IC1_7.3, IC1_7.5, IC1-1.3, IC1-1.5, R6_7.Pin_1, R6_8.Pin_0, C1_7.0, C1_8.0, R4_7.Pin_1, R4_8.Pin_1, C132.1, C133.1, C134.1, C135.0, C136.0, C137.0, C138.1, C139.1, C140.1, C141.0, C142.0, C143.0, C144.1, C145.1, C146.1, C147.0, C148.0, C149.0, T2.S, T2_2.S, T2_3.S, T2_4.S, T2_5.S, T2_6.S, T2_7.S, T2_8.S
  N8: IC5.8, IC1_3.2, IC1_4.1, C107.0, C107.1
  N9: IC5.9, IC4.11, IC1_3.1, IC1_4.2, C109.0, C109.1
  N10: IC5.14, IC4.16, DC1.+Vout, CBUF_4.1, CBUF_5.0
  VIN: IC4.1, DC1.+Vin, DC2.+Vin, Power_Supply.pin17, Power_Supply.pin18, Power_Supply.pin19, Power_Supply.pin20, Power_Supply.pin21, Power_Supply.pin22, Power_Supply.pin23, Power_Supply.pin24, Teensy_3_2.Vin, DIP1_Address.1, DIP1_Address.2, DIP1_Address.3, DIP1_Address.4, DIP1_Address.5, DIP1_Address.6, DIP1_Address.7, DIP1_Address.8, IC2.VCC, CBUF.0, IC3.+V, CBUF_2.0, CBUF_3.1
  N11: IC4.3, Teensy_3_2.D3
  N12: IC4.4, Teensy_3_2.D4
  N13: IC4.5, Teensy_3_2.D5
  N14: IC4.6, Teensy_3_2.D6
  GND: IC4.8, DC1.-Vin, DC2.-Vin, Power_Supply.pin1, Power_Supply.pin2, Power_Supply.pin3, Power_Supply.pin4, Power_Supply.pin5, Power_Supply.pin6, Power_Supply.pin35, Power_Supply.pin36, Power_Supply.pin37, Power_Supply.pin38, Power_Supply.pin39, Power_Supply.pin40, Gen_4.cathode, Gen_3.cathode, Gen_2.cathode, Gen_1.cathode, Power.cathode, Teensy_3_2.GND, R44.Pin_1, R45.Pin_1, RP*1.Pin_1, R46.Pin_1, R47.Pin_1, R48.Pin_1, R7.Pin_1, R50.Pin_1, IC2.E, IC2.GND, CBUF.1, IC3.GND, CBUF_2.1, CBUF_3.0, P1.connector0
  N15: IC1.4, R4.Pin_0
  N16: IC1.6, R3.Pin_1
  N17: IC1.7, DC2.+Vout, IC1_2.7, R1.Pin_0, R1_2.Pin_0, C1.1, C1_2.1, IC1_3.7, IC1_4.7, R1_3.Pin_0, R1_4.Pin_0, C1_3.1, C1_4.1, IC1_5.7, IC1_6.7, R1_5.Pin_0, R1_6.Pin_0, C1_5.1, C1_6.1, IC1_7.7, IC1-1.7, R1_7.Pin_1, R1_8.Pin_0, C1_7.1, C1_8.1
  N18: IC1.11, R5.Pin_1, C2.1, R90.Pin_1, T1.S, T2_4.D
  N19: IC1.12, R2.Pin_1
  N20: IC1.13, C2.0, D1_6.cathode
  N21: IC1_2.4, R4_2.Pin_0
  N22: IC1_2.6, R3_2.Pin_1
  N23: IC1_2.11, R5_2.Pin_0, C2_2.0, R91.Pin_1, T1_2.S, T2_5.D
  N24: IC1_2.12, R2_2.Pin_0
  N25: IC1_2.13, D1.cathode, C2_2.1
  N26: R1.Pin_1, D1_6.anode
  N27: R2.Pin_0, R5.Pin_0, T1.G
  N28: R3.Pin_0, R6.Pin_0, T2_4.G
  N29: R1_2.Pin_1, D1.anode
  N30: R2_2.Pin_1, R5_2.Pin_1, T1_2.G
  N31: R3_2.Pin_0, R6_2.Pin_1, T2_5.G
  N32: Data_Lines.pin1, Data_Lines.pin40, IC3.A
  N33: Data_Lines.pin3, Data_Lines.pin38, IC2.B3
  N34: Data_Lines.pin4, Data_Lines.pin37, IC2.B2
  N35: Data_Lines.pin5, Data_Lines.pin36, IC2.B1
  N36: Data_Lines.pin6, Data_Lines.pin35, IC2.B0
  N37: Data_Lines.pin7, Data_Lines.pin34, IC2.B7
  N38: Data_Lines.pin8, Data_Lines.pin33, IC2.B6
  N39: Data_Lines.pin9, Data_Lines.pin32, IC2.B5
  N40: Data_Lines.pin15, Data_Lines.pin26, Teensy_3_2.A4/D18
  N41: Data_Lines.pin16, Data_Lines.pin25, Teensy_3_2.A5/D19
  N42: Data_Lines.pin17, Data_Lines.pin24, IC2.B4
  N43: Data_Lines.pin18, Data_Lines.pin23, Teensy_3_2.D13
  N44: Data_Lines.pin19, Data_Lines.pin22, Teensy_3_2.D12
  N45: Power_Supply.pin7, Power_Supply.pin8, Power_Supply.pin9, Power_Supply.pin10, Power_Supply.pin11, Power_Supply.pin30, Power_Supply.pin31, Power_Supply.pin32, Power_Supply.pin33, Power_Supply.pin34, J15.pin1
  N46: Power_Supply.pin12, Power_Supply.pin13, Power_Supply.pin14, Power_Supply.pin15, Power_Supply.pin16, Power_Supply.pin25, Power_Supply.pin26, Power_Supply.pin27, Power_Supply.pin28, Power_Supply.pin29, J14.pin1
  N47: J14.pin2, C3.minus, C93.1, C94.1, C95.1, C96.1, C97.1, C98.1, C132.0, C133.0, C134.0, C135.1, C136.1, C137.1, C138.0, C139.0, C140.0, C141.1, C142.1, C143.1, C144.0, C145.0, C146.0, C147.1, C148.1, C149.1, T1.D, T1_2.D, T1_3.D, T1_4.D, T1_5.D, T1_6.D, T1_7.D, T1_8.D
  N48: J14.pin3, J16.pin2
  N49: J15.pin3, J16.pin1
  N50: Gen_4.anode, R8.Pin_0
  N51: Gen_3.anode, R8_2.Pin_0
  N52: Gen_2.anode, R8_3.Pin_0
  N53: Gen_1.anode, R8_4.Pin_0
  N54: Power.anode, R8_5.Pin_0
  N55: R8.Pin_1, Teensy_3_2.A9/D23
  N56: R8_2.Pin_1, Teensy_3_2.A8/D22
  N57: R8_3.Pin_1, Teensy_3_2.A7/D21
  N58: R8_4.Pin_1, Teensy_3_2.D9
  N59: R8_5.Pin_1, Teensy_3_2.3V3, P1.connector2
  N60: Teensy_3_2.D10, IC3.Y
  N61: Teensy_3_2.A0/D14, P1.connector1
  N62: DIP1_Address.9, R7.Pin_0, IC2.A4
  N63: DIP1_Address.10, R48.Pin_0, IC2.A5
  N64: DIP1_Address.11, R50.Pin_0, IC2.A6
  N65: DIP1_Address.12, R47.Pin_0, IC2.A7
  N66: DIP1_Address.13, R46.Pin_0, IC2.A0
  N67: DIP1_Address.14, R44.Pin_0, IC2.A1
  N68: DIP1_Address.15, R45.Pin_0, IC2.A2
  N69: DIP1_Address.16, RP*1.Pin_0, IC2.A3
  N70: IC2.Y, IC3.B
  N71: C99.connector0, v_R9_2.Pin_0
  N72: C99.connector1, v_R9.Pin_0
  N73: C100.connector0, R89.Pin_0
  N74: C100.connector1, R88.Pin_0
  N75: C101.connector0, R91.Pin_0
  N76: C101.connector1, R90.Pin_0
  N77: IC1_3.4, R4_3.Pin_0
  N78: IC1_3.6, R3_3.Pin_1
  N79: IC1_3.11, R5_3.Pin_0, C2_3.0, R92.Pin_1, T1_5.S, T2_8.D
  N80: IC1_3.12, R2_3.Pin_0
  N81: IC1_3.13, D1_2.cathode, C2_3.1
  N82: IC1_4.4, R4_4.Pin_0
  N83: IC1_4.6, R3_4.Pin_1
  N84: IC1_4.11, R5_4.Pin_1, C2_4.1, R93.Pin_1, T1_7.S, T2_6.D
  N85: IC1_4.12, R2_4.Pin_1
  N86: IC1_4.13, D1_3.cathode, C2_4.0
  N87: R2_3.Pin_1, R5_3.Pin_1, T1_5.G
  N88: R2_4.Pin_0, R5_4.Pin_0, T1_7.G
  N89: R3_3.Pin_0, R6_3.Pin_1, T2_8.G
  N90: R3_4.Pin_0, R6_4.Pin_0, T2_6.G
  N91: D1_2.anode, R1_3.Pin_1
  N92: D1_3.anode, R1_4.Pin_1
  N93: IC1_5.4, R4_5.Pin_0
  N94: IC1_5.6, R3_5.Pin_1
  N95: IC1_5.11, R5_5.Pin_0, C2_5.0, R89.Pin_1, T1_8.S, T2_7.D
  N96: IC1_5.12, R2_5.Pin_0
  N97: IC1_5.13, D1_4.cathode, C2_5.1
  N98: IC1_6.4, R4_6.Pin_0
  N99: IC1_6.6, R3_6.Pin_1
  N100: IC1_6.11, R5_6.Pin_1, C2_6.1, R88.Pin_1, T1_4.S, T2_2.D
  N101: IC1_6.12, R2_6.Pin_1
  N102: IC1_6.13, D1_5.cathode, C2_6.0
  N103: R2_5.Pin_1, R5_5.Pin_1, T1_8.G
  N104: R2_6.Pin_0, R5_6.Pin_0, T1_4.G
  N105: R3_5.Pin_0, R6_5.Pin_1, T2_7.G
  N106: R3_6.Pin_0, R6_6.Pin_0, T2_2.G
  N107: D1_4.anode, R1_5.Pin_1
  N108: D1_5.anode, R1_6.Pin_1
  N109: v_R9.Pin_1, IC1_7.11, R5_8.Pin_1, C2_8.1, T1_3.S, T2_3.D
  N110: v_R9_2.Pin_1, IC1-1.11, R5_7.Pin_0, C2_7.1, T2.D, T1_6.S
  N111: R92.Pin_0, C102.connector0
  N112: R93.Pin_0, C102.connector1
  N113: IC1_7.4, R4_7.Pin_0
  N114: IC1_7.6, R3_7.Pin_1
  N115: IC1_7.12, R2_7.Pin_1
  N116: IC1_7.13, C2_8.0, D1_8.cathode
  N117: IC1-1.4, R4_8.Pin_0
  N118: IC1-1.6, R3_8.Pin_1
  N119: IC1-1.12, R2_8.Pin_1
  N120: IC1-1.13, C2_7.0, D1_7.cathode
  N121: R1_7.Pin_0, D1_8.anode
  N122: R1_8.Pin_1, D1_7.anode
  N123: R6_7.Pin_0, R3_7.Pin_0, T2_3.G
  N124: R5_7.Pin_1, R2_8.Pin_0, T1_6.G
  N125: R6_8.Pin_1, R3_8.Pin_0, T2.G
  N126: R5_8.Pin_0, R2_7.Pin_0, T1_3.G

notes:
  -Vin
  +Vin
  -Vout
  +Vout
  < Internal
  External >

custom parts:
  Teensy 3.1: The Teensy is a complete USB-based microcontoller development system, in a very small footprint, capable of implementing many types of projects. All programming is done via the USB port. No special programmer is needed, only a standard micro-USB cable and a PC or Macintosh with a USB port. It has a USB keyboard/mouse/joystick emulation stack and can be programmed through Arduino IDE.
